// Logisim project RS_with_NOR_and_NAND.circ as structural Verilog: 1 circuit, main circuit main
module main (
);

  wire and_1_out, and_2_out, nor_1_out, nor_2_out, undriven, undriven_2, undriven_3, undriven_4;

  nor nor_1 (nor_1_out, undriven, nor_2_out);
  nor nor_2 (nor_2_out, nor_1_out, undriven_2);
  and and_1 (and_1_out, undriven_3, and_2_out);
  and and_2 (and_2_out, and_1_out, undriven_4);

  // Notes on the sheet:
  //   S
  //   R
  //   Q
  //   Q
  //   S
  //   R
  //   Q
  //   Q
endmodule
